# Fritzing sketch schematic2 (saved by Fritzing 1.0.0rc)
breadboards: 1

parts:
  OLED_I2C1 = OLED 128x64 I2C Monochrome Display
  E3Z-R61 = E18-D80NK_1 [mn=or part_number="(NPN NO)" mpn=E3Z-LAS-R8 package=THT]
  Mod2 = Passive Buzzer  # not connected
  S1 = Pushbutton [package="[THT]"]
  R1 = Resistor [tolerance=±5% resistance=10k package="0402 [SMD]"]
  WeMos_D1_Mini1 = WeMos D1 Mini  # not connected

nets:
  N1: OLED_I2C1.VDD, E3Z-R61.pin2, S1.Pin_1, S1.Pin_2
  N2: OLED_I2C1.GND, E3Z-R61.pin1, R1.Pin_1
  N3: S1.Pin_3, S1.Pin_4, R1.Pin_0

custom parts:
  E18-D80NK_1: E18-D80NK Proximity Sensor module.
